// Logisim project 2-1 Mux.circ as structural Verilog: 1 circuit, main circuit main
module main (
  input  X0,
  input  X1,
  input  C,
  output Z
);

  wire and_1_out, and_2_out, not_1_out;

  not not_1 (not_1_out, C);
  and and_1 (and_1_out, not_1_out, X0);
  and and_2 (and_2_out, C, X1);
  or or_1 (Z, and_1_out, and_2_out);
endmodule
