// Logisim project 4-1MUX.circ as structural Verilog: 1 circuit, main circuit main
module main (
  input  X1,
  input  X2,
  input  X3,
  input  X4,
  input  C1,
  input  C2,
  output Z
);

  wire and_1_out, and_2_out, and_3_out, and_4_out, and_5_out, and_6_out, not_1_out, not_2_out, not_3_out,
       or_1_out, or_2_out;

  not not_1 (not_1_out, C1);
  not not_2 (not_2_out, C1);
  and and_1 (and_1_out, X1, C1);
  and and_2 (and_2_out, not_1_out, X2);
  and and_3 (and_3_out, X3, C1);
  and and_4 (and_4_out, not_2_out, X4);
  or or_1 (or_1_out, and_1_out, and_2_out);
  or or_2 (or_2_out, and_3_out, and_4_out);
  and and_5 (and_5_out, or_1_out, C2);
  not not_3 (not_3_out, C2);
  and and_6 (and_6_out, not_3_out, or_2_out);
  or or_3 (Z, and_5_out, and_6_out);

  // Notes on the sheet:
  //   4:1 MUX using 2:1 MUXes
endmodule
