// Logisim project nand_to_nor.circ as structural Verilog: 1 circuit, main circuit main
module main (
  input  in_1,
  input  in_2,
  input  in_3,
  input  in_4,
  input  in_5,
  input  in_6,
  input  in_7,
  input  in_8,
  input  in_9,
  input  in_10,
  input  in_11,
  input  in_12,
  output out_13,
  output out_14,
  output out_15,
  output out_16,
  output out_17,
  output out_18
);

  wire nor_1_out, nor_2_out, nor_3_out, nor_4_out, nor_5_out, nor_6_out, nor_7_out, nor_8_out, nor_9_out,
       nor_10_out, nor_11_out, nor_12_out;

  xor xor_1 (out_13, in_2, in_3);
  xor xor_2 (out_15, in_6, in_7);
  xor xor_3 (out_17, in_10, in_11);
  nor nor_1 (nor_1_out, in_1, in_1);
  nor nor_2 (nor_2_out, in_4, in_4);
  nor nor_3 (nor_3_out, in_4, in_1);
  nor nor_4 (nor_4_out, in_5, in_5);
  nor nor_5 (nor_5_out, in_8, in_8);
  nor nor_6 (nor_6_out, in_8, in_5);
  nor nor_7 (nor_7_out, in_9, in_9);
  nor nor_8 (nor_8_out, in_12, in_12);
  nor nor_9 (nor_9_out, in_12, in_9);
  nor nor_10 (nor_10_out, nor_1_out, nor_2_out);
  nor nor_11 (nor_11_out, nor_4_out, nor_5_out);
  nor nor_12 (nor_12_out, nor_7_out, nor_8_out);
  nor nor_13 (out_14, nor_10_out, nor_3_out);
  nor nor_14 (out_16, nor_11_out, nor_6_out);
  nor nor_15 (out_18, nor_12_out, nor_9_out);

  // Notes on the sheet:
  //   XOR
  //   NOR
endmodule
