// Logisim project nor_to_nand.circ as structural Verilog: 1 circuit, main circuit main
module main (
  input  in_1,
  input  in_2,
  input  in_3,
  input  in_4,
  input  in_5,
  input  in_6,
  input  in_7,
  input  in_8,
  input  in_9,
  input  in_10,
  input  in_11,
  input  in_12,
  output out_13,
  output out_14,
  output out_15,
  output out_16,
  output out_17,
  output out_18
);

  wire nand_1_out, nand_2_out, nand_3_out, nand_4_out, nand_5_out, nand_6_out, nand_7_out, nand_8_out,
       nand_9_out;

  nor nor_1 (out_14, in_2, in_3);
  nor nor_2 (out_15, in_6, in_7);
  nor nor_3 (out_17, in_10, in_11);
  nand nand_1 (nand_1_out, in_1, in_1);
  nand nand_2 (nand_2_out, in_4, in_4);
  nand nand_3 (nand_3_out, in_5, in_5);
  nand nand_4 (nand_4_out, in_8, in_8);
  nand nand_5 (nand_5_out, in_9, in_9);
  nand nand_6 (nand_6_out, in_12, in_12);
  nand nand_7 (nand_7_out, nand_1_out, nand_2_out);
  nand nand_8 (nand_8_out, nand_3_out, nand_4_out);
  nand nand_9 (nand_9_out, nand_5_out, nand_6_out);
  nand nand_10 (out_13, nand_7_out, nand_7_out);
  nand nand_11 (out_16, nand_8_out, nand_8_out);
  nand nand_12 (out_18, nand_9_out, nand_9_out);

  // Notes on the sheet:
  //   NOR
  //   NAND
endmodule
